# Fritzing sketch rc-raspi-circuit (saved by Fritzing 0.9.4)

parts:
  Raspberry_Pi_1 = Raspberry Pi 3 [part_number=RPI-3-V1.2]
  2_Channel_Relay1 = 2 Channel Power Relay
  S1 = KY-026
  DHT1 = Humidity and Temperature Sensor DHT11

nets:
  3V3: Raspberry_Pi_1.3v3, DHT1.Vcc
  N1: Raspberry_Pi_1.GIPO17, 2_Channel_Relay1.IN1
  N2: Raspberry_Pi_1.GIPO27, S1.pin4
  N3: Raspberry_Pi_1.GIPO25, DHT1.Data-signal
  GND: Raspberry_Pi_1.GND, 2_Channel_Relay1.GND, S1.pin2, DHT1.GND_1
  N4: Raspberry_Pi_1.GIPO18, 2_Channel_Relay1.IN2
  5V: Raspberry_Pi_1.5V, 2_Channel_Relay1.VCC, S1.pin3

custom parts:
  2 Channel Power Relay: A 2 channel power relay. The module operates at 5V.
  KY-026: ky-026 flame sensor module
  Humidity and Temperature Sensor DHT11: Digital relative humidity & temperature sensor DHT11
